# Fritzing sketch circuit (saved by Fritzing 0.9.3b)
breadboards: 3

parts:
  Part1 = Arduino Mega 2560 (Rev3)
  S1 = H-Bridge with L298N
  M1 = DC Motor
  M2 = DC Motor
  M3 = DC Motor
  M4 = DC Motor
  VCC1 = Battery block 9V
  Part2 = RFID-RC522-v2
  S2 = SWITCH-DPDT-latching [package=os]
  S3 = SWITCH-DPDT-latching [package=os]
  J1 = Piezo Speaker
  J2 = Piezo Speaker
  LED1 = smd LED [color="Red (633nm)" package="0603 [SMD]"]
  LED2 = smd LED [color="Green (570nm)" package="0603 [SMD]"]
  R1 = Resistor [tolerance=±5% resistance=100 package=THT]
  R2 = Resistor [tolerance=±5% resistance=100 package=THT]
  YL-83_-_Detection_Board1 = YL-83 Rain Sensor - Detection Board
  YL-83_-_Control_Board1 = YL-83 Rain Sensor - Control Board
  Water_Level_Sensor1 = Water Level Sensor
  Part4 = Bluetooth HC-05 Macho
  LED3 = smd LED [color="Red (633nm)" package="0603 [SMD]"]
  J3 = Basic Servo
  Part5 = Thumb Joystick
  LCD1 = LCD screen
  Part6 = KY-033 Tracing Black White Line Hunting Sensor Module For Arduino
  Part7 = KY-033 Tracing Black White Line Hunting Sensor Module For Arduino

nets:
  N1: Part1.A0, Water_Level_Sensor1.SIG
  N2: Part1.A1, YL-83_-_Control_Board1.AO
  N3: Part1.A2, Part5.HORZ
  N4: Part1.D14/TX3, Part4.RXD
  N5: Part1.D13_PWM, Part4.TXD
  N6: Part1.D12_PWM, J3.pulse
  N7: Part1.D11_PWM, LCD1.LED+
  N8: Part1.D10_PWM, LCD1.V0
  N9: Part1.D9_PWM, S1.ENB
  N10: Part1.D8_PWM, S1.ENA
  3V3: Part1.3V3, Part2.3.3V
  VCC: Part1.5V, S2.1, S2.6, S3.1, S3.6, R1.Pin_0, YL-83_-_Control_Board1.VCC, Water_Level_Sensor1.VCC, Part4.VCC, Part5.VERT, Part5.VCC, LCD1.VDD, Part6.V+, Part7.V+
  GND: Part1.GND, S1.GND, VCC1.-, Part2.GND, S2.3, S2.4, S3.3, S3.4, J1.pin1, J2.pin1, R2.Pin_0, YL-83_-_Control_Board1.GND, Water_Level_Sensor1.GND, Part4.GND, LED3.anode, J3.gnd, Part5.GND, LCD1.VSS, LCD1.R/W, LCD1.LED-, Part6.GND, Part7.GND
  VIN: Part1.VIN, S1.12V, VCC1.+, J3.vcc
  N11: Part1.D7_PWM, LED3.cathode
  N12: Part1.D22, S1.IN2
  N13: Part1.D23, S1.IN1
  N14: Part1.D24, S1.IN3
  N15: Part1.D25, S1.IN4
  N16: Part1.D26, LCD1.E
  N17: Part1.D28, LCD1.RS
  N18: Part1.D29, J1.pin2
  N19: Part1.D31, J2.pin2
  N20: Part1.D33, S2.2, S2.5
  N21: Part1.D35, S3.2, S3.5
  N22: Part1.D36, LCD1.DB7
  N23: Part1.D37, Part6.S
  N24: Part1.D38, LCD1.DB6
  N25: Part1.D40, LCD1.DB5
  N26: Part1.D42, LCD1.DB4
  N27: Part1.D43, Part7.S
  N28: Part1.D48, LED1.cathode, LED2.anode
  N29: Part1.D49, Part2.RST
  N30: Part1.D50, Part2.MISO
  N31: Part1.D51, Part2.MOSI
  N32: Part1.D52, Part2.SCK
  N33: Part1.D53, Part2.SDA
  N34: S1.M1-01, M1.pin_1, M3.pin_2
  N35: S1.M1-02, M1.pin_2, M3.pin_1
  N36: S1.M2-01, M2.pin_2, M4.pin_1
  N37: S1.M2-02, M2.pin_1, M4.pin_2
  N38: LED1.anode, R1.Pin_1
  N39: LED2.cathode, R2.Pin_1
  N40: YL-83_-_Detection_Board1.POS, YL-83_-_Control_Board1.POS
  N41: YL-83_-_Detection_Board1.NEG, YL-83_-_Control_Board1.NEG

notes:
  Right Motors
  Left Motors

custom parts:
  H-Bridge with L298N: h-bridge
  RFID-RC522-v2: A simple China made RFID-RC522 Reader; do check the pin labels, as this is a MFRC522 based clone.
  SWITCH-DPDT-latching: DPDT latching pushbutton switch
  YL-83 Rain Sensor - Detection Board: The YL-83 is a rain sensor that has more resistance when dry and less resistance when wet. The module runs at 5V.
  YL-83 Rain Sensor - Control Board: The YL-83 is a rain sensor that has more resistance when dry and less resistance when wet. The module runs at 5V.
  Water Level Sensor: A water level sensor. This sensor operates at 3V to 5V. The Sig (signal) pin outputs an analogue signal that is in proportion to the amount of water in contact with the sensor.
  KY-033 Tracing Black White Line Hunting Sensor Module For Arduino: Tracing Black White Line Hunting Sensor Module For Arduino Description: This is KY-033 tracking sensor. The KY-033 measures the intensity of infrared radiation and delivers it as an analog output voltage. Features: Operating voltage: 2.5 - 12V(cannot over12V) working current: 18mA-20mA at 5V Enhanced accuracy Documents: http://www.vishay.com/docs/83760/tcrt5000.pdf
